# Fritzing sketch radio (saved by Fritzing 0.9.0b)
circuit board: 8.46667cm x 5.64444cm
breadboards: 1

parts:
  Part1 = Arduino Pro Mini v13
  Part2 = DeadOn RTC - DS3234 Breakout
  Part3 = Digital FM Radio Receiver
  BB1 = 4-Line Bi-Directional Level Shifter
  LCD1 = ST7565 128x64 RGB Backlight [part_number=438]
  Part4 = ST2012 2.8W Class D Stereo Amplifier
  neopixel2 = Neopixel 60 Ring
  R1 = 100 Ω Resistor [package=THT]
  R2 = 100 Ω Resistor [package=THT]
  R3 = 100 Ω Resistor [package=THT]

nets:
  N1: Part1.A4, Part3.SDIO
  N2: Part1.A5, Part3.SCLK
  VDD: Part1.RAW, BB1.HV, Part4.VDD, neopixel2.5v
  GND: Part1.GND, Part2.GND, Part3.GND, BB1.GND, LCD1.GND, Part4.GND, neopixel2.gnd
  VCC: Part1.VCC, Part2.VCC, Part3.3.3V, BB1.LV, LCD1.VDD, LCD1.A+
  N3: Part1.A0, BB1.A1
  N4: Part1.D13/SCK, Part2.SCLK, LCD1.SCLK
  N5: Part1.D12/MISO, Part2.MISO
  N6: Part1.D11_PWM/MOSI, Part2.MOSI, LCD1.SID
  N7: Part1.D10_PWM/SS, Part2.SS
  N8: Part1.D8, Part3.!RST
  N9: Part1.D7, LCD1./CS
  N10: Part1.D6_PWM, R3.Pin_1
  N11: Part1.D5_PWM, R1.Pin_1
  N12: Part1.D4, LCD1./RST
  N13: Part1.D3_PWM, R2.Pin_1
  N14: Part1.D2, LCD1.A0
  N15: BB1.B1, neopixel2.din
  N16: LCD1.R-, R2.Pin_0
  N17: LCD1.G-, R1.Pin_0
  N18: LCD1.B-, R3.Pin_0

custom parts:
  4-Line Bi-Directional Level Shifter: 4-Channel Bi-Directional Level Shifter
  ST7565 128x64 RGB Backlight: 128x64 RGB Backlight
  Neopixel 60 Ring: Neopixel 60 Ring Fully assembeled quarter rings
  100 Ω Resistor: A generic resistor (0.25W)
