# Fritzing sketch radio_protoboard (saved by Fritzing 0.9.0b)
circuit board: 8.46667cm x 5.64444cm
breadboards: 1
perfboards: 1

parts:
  Part1 = Arduino Pro Mini v13
  Part2 = DeadOn RTC - DS3234 Breakout
  Part3 = Digital FM Radio Receiver
  BB1 = 4-Line Bi-Directional Level Shifter
  LCD1 = ST7565 128x64 RGB Backlight [part_number=438]
  Part4 = ST2012 2.8W Class D Stereo Amplifier
  neopixel2 = Neopixel 60 Ring
  R1 = 100 Ω Resistor [package=THT]
  R2 = 100 Ω Resistor [package=THT]
  R3 = 100 Ω Resistor [package=THT]
  J1 = female pin header, 7 pins [form="♀ (female)"]  # not connected
  LCD2 = ST7565 128x64 RGB Backlight [part_number=438]  # not connected
  J6 = female pin header, 10 pins [form="♀ (female)" part_number="audio amp"]
  J8 = female pin header, 10 pins [form="♀ (female)" part_number="fm receiver"]  # not connected
  J9 = double row female pin header, 12 pins [form="♀ (female)"]  # not connected
  J10 = double row female pin header, 12 pins [form="♀ (female)"]  # not connected
  J4 = double row male pin header, 2 pins [form="♂ (male)" part_number="io lcd"]  # not connected
  J2 = male pin header, 2 pins [form="♂ (male)" part_number="pwr lcd"]  # not connected
  J3 = male pin header, 4 pins [form="♂ (male)" part_number="backlight lcd"]  # not connected
  J5 = male pin header, 3 pins [form="♂ (male)" part_number="io aux lcd"]  # not connected
  J7 = male pin header, 3 pins [form="♂ (male)" part_number="neo pixel"]  # not connected
  J11 = female pin header, 6 pins [form="♀ (female)"]  # not connected
  J12 = female pin header, 6 pins [form="♀ (female)"]  # not connected
  J7_2 = single row smd female pin header, 6 pins [form="♀ (female)"]  # not connected
  J13 = male pin header, 2 pins [form="♂ (male)" part_number="fm i2c"]  # not connected
  J14 = male pin header, 2 pins [form="♂ (male)" part_number="5V pwr in"]  # not connected
  R7 = Resistor [tolerance=±5% resistance=330 package=THT]  # not connected
  R8 = Resistor [tolerance=±5% resistance=330 package=THT]  # not connected
  R9 = Resistor [tolerance=±1% resistance=100 package=THT]  # not connected

nets (from the breadboard view):
  N1: Part1.A4, Part3.SDIO
  N2: Part1.A5, Part3.SCLK
  VDD: Part1.RAW, BB1.HV, Part4.VDD, neopixel2.5v
  GND: Part1.GND, Part2.GND, Part3.GND, BB1.GND, LCD1.GND, Part4.GND, neopixel2.gnd
  VCC: Part1.VCC, Part2.VCC, Part3.3.3V, BB1.LV
  N3: Part1.A0, Part3.!RST
  N4: Part1.D13/SCK, Part2.SCLK, LCD1.SCLK
  N5: Part1.D12/MISO, Part2.MISO
  N6: Part1.D11_PWM/MOSI, Part2.MOSI, LCD1.SID
  N7: Part1.D10_PWM/SS, Part2.SS
  N8: Part1.D8, BB1.A1
  N9: Part1.D7, LCD1./CS
  N10: Part1.D6_PWM, R3.Pin_1
  N11: Part1.D5_PWM, R1.Pin_1
  N12: Part1.D4, LCD1./RST
  N13: Part1.D3_PWM, R2.Pin_1
  N14: Part1.D2, LCD1.A0
  N15: BB1.B1, neopixel2.din
  N16: LCD1.VDD, LCD1.A+
  N17: LCD1.R-, R2.Pin_0
  N18: LCD1.G-, R1.Pin_0
  N19: LCD1.B-, R3.Pin_0
  N20: J6.pin5, J6.pin6

custom parts:
  4-Line Bi-Directional Level Shifter: 4-Channel Bi-Directional Level Shifter
  ST7565 128x64 RGB Backlight: 128x64 RGB Backlight
  Neopixel 60 Ring: Neopixel 60 Ring Fully assembeled quarter rings
  100 Ω Resistor: A generic resistor (0.25W)
